# Fritzing sketch Switcher-sketch (saved by Fritzing 0.9.3b)
breadboards: 3

parts:
  Part1 = Arduino Nano (Rev3.0) (ICSP)
  S2 = SWITCH-MOMENTARY-2 [package=tactile-pth-12mm]
  S1 = SWITCH-MOMENTARY-2 [package=tactile-pth-12mm]
  S3 = SWITCH-MOMENTARY-2 [package=tactile-pth-12mm]
  S4 = SWITCH-MOMENTARY-2 [package=tactile-pth-12mm]
  S5 = SWITCH-MOMENTARY-2 [package=tactile-pth-12mm]
  R1 = Resistor [tolerance=±5% resistance=1k package=THT]
  R2 = Resistor [tolerance=±5% resistance=1k package=THT]
  R3 = Resistor [tolerance=±5% resistance=1k package=THT]
  R4 = Resistor [tolerance=±5% resistance=1k package=THT]
  R5 = Resistor [tolerance=±5% resistance=1k package=THT]
  S6 = SWITCH-MOMENTARY-2 [package=tactile-pth-12mm]
  R6 = Resistor [tolerance=±5% resistance=1k package=THT]
  S7 = SWITCH-MOMENTARY-2 [package=tactile-pth-12mm]
  R7 = Resistor [tolerance=±5% resistance=1k package=THT]
  S8 = SWITCH-MOMENTARY-2 [package=tactile-pth-12mm]
  R8 = Resistor [tolerance=±5% resistance=1k package=THT]
  R10 = Rotary Potentiometer (Small) [maximum_resistance=20kΩ package=THT]
  R11 = Rotary Potentiometer (Small) [maximum_resistance=20kΩ package=THT]
  R12 = Rotary Potentiometer (Small) [maximum_resistance=20kΩ package=THT]
  R13 = Rotary Potentiometer (Small) [maximum_resistance=20kΩ package=THT]
  R14 = Rotary Potentiometer (Small) [maximum_resistance=20kΩ package=THT]
  S9 = SWITCH-MOMENTARY-2 [package=tactile-pth-12mm]
  R9 = Resistor [tolerance=±5% resistance=1k package=THT]

nets:
  N1: Part1.GND, R1.Pin_0, R2.Pin_0, R3.Pin_0, R5.Pin_0, R6.Pin_0, R7.Pin_0, R10.leg1, R11.leg1, R12.leg1, R13.leg1, R14.leg1, R9.Pin_0
  N2: Part1.D2, S1.1, R1.Pin_1
  N3: Part1.D3, S2.1, R2.Pin_1
  N4: Part1.D4, S3.1, R3.Pin_1
  N5: Part1.D5, S4.1, R4.Pin_1
  N6: Part1.D6, S5.1, R5.Pin_1
  N7: Part1.D7, S6.1, R6.Pin_1
  N8: Part1.D8, S7.1, R7.Pin_1
  N9: Part1.D9, S8.1, R8.Pin_1
  N10: Part1.D10, S9.1, R9.Pin_1
  N11: Part1.5V, R10.leg2, R11.leg2, R12.leg2, R13.leg2, R14.leg2
  N12: Part1.A4, R14.wiper
  N13: Part1.A3, R13.wiper
  N14: Part1.A2, R12.wiper
  N15: Part1.A1, R11.wiper
  N16: Part1.A0, R10.wiper
